// Logisim project control-logic.circ as structural Verilog: 1 circuit, main circuit control_logic
module control_logic (
  input  [31:0] Instruction,
  input  BrEq,
  input  BrLt,
  output PCSel,
  output RegWEn,
  output [2:0] ImmSel,
  output BrUn,
  output ASel,
  output BSel,
  output [3:0] ALUSel,
  output MemRW,
  output [1:0] WBSel
);

  wire and_1_out, and_2_out, and_3_out, and_4_out, and_7_out, and_8_out, and_9_out, and_10_out, and_11_out,
       and_12_out, and_13_out, and_14_out, and_15_out, auipc, Btype, comparator_10_eq, comparator_11_eq,
       comparator_12_eq, comparator_13_eq, jal, jalr, Ltype, lui, not_7_out, not_8_out, not_9_out,
       not_10_out, not_11_out, not_12_out, not_13_out, or_1_out, or_4_out, or_5_out, or_12_out, or_13_out,
       RItype, Rtype;
  wire [2:0] and_5_out, bit_extender_1_out, bit_extender_2_out, bit_extender_3_out, bit_extender_4_out,
       bit_extender_5_out, bit_extender_6_out, bit_extender_7_out, bit_extender_8_out, multiplexer_1_out,
       not_1_out, not_2_out, not_3_out, not_4_out, not_5_out, not_6_out, or_2_out;

  Comparator #(.width(5)) comparator_1 (.a(Instruction[6:2]), .b(5'b00100), .eq(RItype));  // open: gt, lt
  Comparator #(.width(5)) comparator_2 (.a(Instruction[6:2]), .b(5'b01100), .eq(Rtype));  // open: gt, lt
  Comparator #(.width(5)) comparator_3 (.a(Instruction[6:2]), .b(5'b11000), .eq(Btype));  // open: gt, lt
  Comparator #(.width(5)) comparator_4 (.a(Instruction[6:2]), .b(5'b01111), .eq(MemRW));  // open: gt, lt
  Comparator #(.width(5)) comparator_5 (.a(Instruction[6:2]), .b({5{1'b0}}), .eq(Ltype));  // open: gt, lt
  Comparator #(.width(5)) comparator_6 (.a(Instruction[6:2]), .b(5'b00101), .eq(auipc));  // open: gt, lt
  Comparator #(.width(5)) comparator_7 (.a(Instruction[6:2]), .b(5'b01101), .eq(lui));  // open: gt, lt
  Comparator #(.width(5)) comparator_8 (.a(Instruction[6:2]), .b(5'b11011), .eq(jal));  // open: gt, lt
  Comparator #(.width(5)) comparator_9 (.a(Instruction[6:2]), .b(5'b11001), .eq(jalr));  // open: gt, lt
  Comparator #(.width(3)) comparator_10 (.a(Instruction[14:12]), .b(3'b000), .eq(comparator_10_eq));  // open: gt, lt
  Comparator #(.mode("unsigned"), .width(3)) comparator_11 (
    .a(Instruction[14:12]), .b(3'b101), .eq(comparator_11_eq));  // open: gt, lt
  Comparator #(.mode("unsigned"), .width(3)) comparator_12 (
    .a(Instruction[14:12]), .b(3'b000), .eq(comparator_12_eq));  // open: gt, lt
  and and_1 (and_1_out, Instruction[25], Rtype);
  Multiplexer #(.width(3)) multiplexer_1 (
    .in0(Instruction[14:12]), .in1(3'b100), .out(multiplexer_1_out), .sel(and_2_out));
  and and_2 (and_2_out, comparator_10_eq, Rtype, Instruction[30]);
  assign bit_extender_1_out = {{2{jal}}, jal};  // Bit_Extender bit_extender_1
  assign bit_extender_2_out = {{2{jalr}}, jalr};  // Bit_Extender bit_extender_2
  Comparator #(.mode("unsigned"), .width(3)) comparator_13 (
    .a(Instruction[14:12]), .b(3'b101), .eq(comparator_13_eq));  // open: gt, lt
  or or_1 (or_1_out, comparator_11_eq, comparator_12_eq);
  assign bit_extender_3_out = {{2{auipc}}, auipc};  // Bit_Extender bit_extender_3
  assign bit_extender_4_out = {{2{lui}}, lui};  // Bit_Extender bit_extender_4
  assign bit_extender_5_out = {{2{Btype}}, Btype};  // Bit_Extender bit_extender_5
  assign bit_extender_6_out = {{2{Ltype}}, Ltype};  // Bit_Extender bit_extender_6
  assign bit_extender_7_out = {{2{MemRW}}, MemRW};  // Bit_Extender bit_extender_7
  assign or_2_out = bit_extender_1_out | bit_extender_2_out;  // OR_Gate or_2, 3 bits wide
  assign not_1_out = ~or_2_out;  // NOT_Gate not_1, 3 bits wide
  and and_3 (and_3_out, Instruction[30], RItype, comparator_13_eq);
  and and_4 (and_4_out, Instruction[30], Rtype, or_1_out);
  assign not_2_out = ~bit_extender_3_out;  // NOT_Gate not_2, 3 bits wide
  assign not_3_out = ~bit_extender_4_out;  // NOT_Gate not_3, 3 bits wide
  assign not_4_out = ~bit_extender_5_out;  // NOT_Gate not_4, 3 bits wide
  assign not_5_out = ~bit_extender_6_out;  // NOT_Gate not_5, 3 bits wide
  assign not_6_out = ~bit_extender_7_out;  // NOT_Gate not_6, 3 bits wide
  or or_3 (ALUSel[3], and_3_out, and_4_out, and_1_out, lui);
  assign and_5_out = not_2_out & multiplexer_1_out & not_3_out & not_4_out & not_5_out & not_6_out & not_1_out;  // AND_Gate and_5, 3 bits wide
  assign bit_extender_8_out = {{2{lui}}, lui};  // Bit_Extender bit_extender_8
  or or_4 (or_4_out, RItype, jalr, Ltype);
  or or_5 (or_5_out, auipc, lui);
  or or_6 (RegWEn, jal, Ltype, auipc, Rtype, lui, RItype, jalr);
  or or_7 (ASel, auipc, Btype, jal);
  or or_8 (BSel, jal, auipc, Ltype, Btype, MemRW, RItype, lui, jalr);
  and and_6 (BrUn, Btype, Instruction[13]);
  or or_9 (WBSel[0], RItype, auipc, Rtype, lui, 1'b0);
  or or_10 (WBSel[1], jalr, jal);
  assign ALUSel[2:0] = and_5_out | bit_extender_8_out;  // OR_Gate or_11, 3 bits wide
  Priority_Encoder priority_encoder_1 (
    .in0(or_4_out), .in1(MemRW), .in2(Btype), .in3(or_5_out), .in4(jal), .out(ImmSel));  // open: in5, in6, in7, en_in, gs, en_out
  not not_7 (not_7_out, Instruction[12]);
  not not_8 (not_8_out, Instruction[14]);
  not not_9 (not_9_out, Instruction[14]);
  not not_10 (not_10_out, BrEq);
  and and_7 (and_7_out, Instruction[12], not_9_out);
  not not_11 (not_11_out, Instruction[12]);
  not not_12 (not_12_out, BrEq);
  not not_13 (not_13_out, BrLt);
  and and_8 (and_8_out, not_7_out, not_8_out);
  and and_9 (and_9_out, not_10_out, and_7_out);
  and and_10 (and_10_out, not_11_out, Instruction[14]);
  or or_12 (or_12_out, not_12_out, not_13_out);
  and and_11 (and_11_out, Instruction[12], Instruction[14]);
  and and_12 (and_12_out, BrEq, and_8_out);
  and and_13 (and_13_out, BrLt, and_10_out);
  and and_14 (and_14_out, or_12_out, and_11_out);
  or or_13 (or_13_out, and_12_out, and_9_out, and_13_out, and_14_out);
  and and_15 (and_15_out, Btype, or_13_out);
  or or_14 (PCSel, jal, and_15_out, jalr);

  // Other names for the same wires on the sheet: opcode[4:0] = Instruction[6:2]; func3[2:0] = Instruction[14:12];
  //   func3_1 = Instruction[12]; func3_2 = Instruction[13]; func3_3 = Instruction[14];
  //   func7[6:0] = Instruction[31:25]; func725 = Instruction[25]; func730 = Instruction[30]; Stype = MemRW

  // Notes on the sheet:
  //   INPUTS to your circuit
  //   DON'T CHANGE THE LOCATIONS OF THE INPUTS AND OUTPUTS!
  //   OUTPUT from your circuit
endmodule
