// Logisim project cpu.circ as structural Verilog: 1 circuit, main circuit cpu
module cpu (
  input  clk,
  input  [31:0] Instruction,
  input  [31:0] MemReadData,
  output [31:0] MemAddress,
  output [31:0] ProgramCounter,
  output [31:0] ra,
  output [31:0] sp,
  output [31:0] t0,
  output [31:0] t1,
  output [31:0] t2,
  output [31:0] s0,
  output [31:0] s1,
  output [31:0] a0,
  output [3:0] MemWriteMask,
  output [31:0] MemWriteData
);

  wire ASel, BrEq, BrLt, BrUn, BSel, MemRW, PCSel, PCSel2, RegWEn, undriven;
  wire [1:0] WBSel;
  wire [2:0] ImmSel;
  wire [3:0] ALUSel;
  wire [31:0] Immediate, Instruction_t, MemToReg, multiplexer_1_out, multiplexer_2_out, multiplexer_4_out,
       multiplexer_5_out, pc4, pc41, ProgramCounter_t, ReadData1, ReadData2, register_3_q;

  // Probe on pc41
  Adder #(.width(32)) adder_1 (.a(ProgramCounter), .b(32'h4), .out(pc41));  // open: cin, cout
  // Probe on pc41
  // Probe on ProgramCounter
  Multiplexer #(.width(32)) multiplexer_1 (.in0(pc41), .in1(MemAddress), .out(multiplexer_1_out), .sel(PCSel));
  // Probe on Instruction
  Register #(.width(32)) register_1 (.D(pc41), .en(1'b1), .clk(clk), .Q(pc4));  // open: clr
  Register #(.width(32)) register_2 (.D(ProgramCounter), .en(1'b1), .clk(clk), .Q(ProgramCounter_t));  // open: clr
  control_logic control_logic_1 (
    .Instruction(Instruction_t), .BrEq(BrEq), .BrLt(BrLt), .PCSel(PCSel), .RegWEn(RegWEn), .ImmSel(ImmSel),
    .BrUn(BrUn), .ASel(ASel), .BSel(BSel), .ALUSel(ALUSel), .MemRW(MemRW), .WBSel(WBSel));
  // Probe on multiplexer_1_out
  Register #(.width(32)) register_3 (.D(Instruction), .en(1'b1), .clk(clk), .Q(register_3_q), .clr(undriven));
  Register #(.width(32)) PC (.D(multiplexer_1_out), .en(1'b1), .clk(clk), .Q(ProgramCounter));  // open: clr
  Multiplexer #(.select(2), .width(32)) multiplexer_2 (
    .in0(MemToReg), .in1(MemAddress), .in2(pc4), .out(multiplexer_2_out), .sel(WBSel));  // open: in3
  Multiplexer #(.width(32)) multiplexer_3 (.in0(register_3_q), .in1(32'h13), .out(Instruction_t), .sel(PCSel2));
  Register #(.width(1)) register_4 (.D(PCSel), .en(1'b1), .clk(clk), .Q(PCSel2));  // open: clr
  regfile regfile_1 (
    .ReadIndex1(Instruction_t[19:15]), .ReadIndex2(Instruction_t[24:20]), .WriteIndex(Instruction_t[11:7]),
    .WriteData(multiplexer_2_out), .RegWEn(RegWEn), .clk(clk), .ra(ra), .sp(sp), .t0(t0), .t1(t1), .t2(t2),
    .s0(s0), .s1(s1), .a0(a0), .ReadData1(ReadData1), .ReadData2(ReadData2));
  imm_gen imm_gen_1 (.Instruction(Instruction_t), .ImmSel(ImmSel), .Immediate(Immediate));
  Multiplexer #(.width(32)) multiplexer_4 (
    .in0(ReadData1), .in1(ProgramCounter_t), .out(multiplexer_4_out), .sel(ASel));
  Multiplexer #(.width(32)) multiplexer_5 (.in0(ReadData2), .in1(Immediate), .out(multiplexer_5_out), .sel(BSel));
  alu alu_1 (.A(multiplexer_4_out), .B(multiplexer_5_out), .ALUSel(ALUSel), .ALUResult(MemAddress));
  branch_comp branch_comp_1 (.BrData1(ReadData1), .BrData2(ReadData2), .BrUn(BrUn), .BrEq(BrEq), .BrLt(BrLt));
  partial_store partial_store_1 (
    .Instruction(Instruction_t), .MemAddress(MemAddress), .DataFromReg(ReadData2), .MemRW(MemRW),
    .MemWriteMask(MemWriteMask), .DataToMem(MemWriteData));
  partial_load partial_load_1 (
    .Instruction(Instruction_t), .MemAddress(MemAddress), .DataFromMem(MemReadData), .DataToReg(MemToReg));

  // Other names for the same wires on the sheet: Instruction1[31:0] = Instruction; rd[4:0] = Instruction_t[11:7];
  //   rs1[4:0] = Instruction_t[19:15]; rs2[4:0] = Instruction_t[24:20]; ProgramCounter1[31:0] = ProgramCounter

  // Notes on the sheet:
  //   To IMEM
  //   IMEM (do **NOT** move this)
  //   From IMEM
  //   Inputs/Outputs for testing. Do **NOT** move these.
  //   To DMEM
  //   DMEM (do **NOT** move this)
  //   From DMEM
endmodule
