// Logisim project imm-gen.circ as structural Verilog: 1 circuit, main circuit imm_gen
module imm_gen (
  input  [31:0] Instruction,
  input  [2:0] ImmSel,
  output [31:0] Immediate
);

  wire [31:0] Btype, Itype, Jtype, Stype;

  assign Itype = {{20{Instruction[31]}}, Instruction[31:20]};  // Bit_Extender bit_extender_1
  assign Stype = {{20{Instruction[31]}}, {Instruction[31:25], Instruction[11:7]}};  // Bit_Extender bit_extender_2
  assign Btype = {{19{Instruction[31]}}, {Instruction[31], Instruction[7], Instruction[30:25], Instruction[11:8], 1'b0}};  // Bit_Extender bit_extender_3
  assign Jtype = {{11{Instruction[31]}}, {Instruction[31], Instruction[19:12], Instruction[20], Instruction[30:21], 1'b0}};  // Bit_Extender bit_extender_4
  Multiplexer #(.select(3), .width(32)) multiplexer_1 (
    .in0(Itype), .in1(Stype), .in2(Btype), .in3({Instruction[31:12], {12{1'b0}}}), .in4(Jtype),
    .out(Immediate), .sel(ImmSel));  // open: in5, in6, in7
  Multiplexer #(.select(3), .width(32)) multiplexer_2 (.sel(ImmSel));  // open: in0, in1, in2, in3, in4, in5, in6, in7, out

  // Other names for the same wires on the sheet: Ins8_11[3:0] = Instruction[11:8]; Ins7 = Instruction[7];
  //   Ins21_24[3:0] = Instruction[24:21]; Utype[31:12] = Instruction[31:12]; Ins25 = Instruction[25];
  //   Ins25_30[5:0] = Instruction[30:25]; Ins26_30[4:0] = Instruction[30:26]; Ins20 = Instruction[20];
  //   Ins12_19[7:0] = Instruction[19:12]; Ins31 = Instruction[31]

  // Notes on the sheet:
  //   INPUTS to your circuit
  //   DON'T CHANGE THE LOCATIONS OF THE INPUTS AND OUTPUTS!
  //   OUTPUT from your circuit
endmodule
