// Logisim project partial-store.circ as structural Verilog: 1 circuit, main circuit partial_store
module partial_store (
  input  [31:0] Instruction,
  input  [31:0] MemAddress,
  input  [31:0] DataFromReg,
  input  MemRW,
  output [3:0] MemWriteMask,
  output [31:0] DataToMem
);

  wire [3:0] bit_extender_3_out, multiplexer_6_out, sbmask, shmask;
  wire [31:0] bit_extender_1_out, bit_extender_2_out, sb, sh, shifter_1_out, shifter_2_out, shifter_3_out,
       shifter_4_out, shifter_5_out;

  assign bit_extender_1_out = {{24{1'b0}}, DataFromReg[7:0]};  // Bit_Extender bit_extender_1
  assign bit_extender_2_out = {{16{1'b0}}, DataFromReg[15:0]};  // Bit_Extender bit_extender_2
  Shifter #(.width(32)) shifter_1 (.in(bit_extender_1_out), .\dist (5'b01000), .out(shifter_1_out));
  Shifter #(.width(32)) shifter_2 (.in(bit_extender_1_out), .\dist (5'b10000), .out(shifter_2_out));
  Shifter #(.width(32)) shifter_3 (.in(bit_extender_1_out), .\dist (5'b11000), .out(shifter_3_out));
  Multiplexer #(.select(2), .width(32)) multiplexer_1 (
    .in0(bit_extender_1_out), .in1(shifter_1_out), .in2(shifter_2_out), .in3(shifter_3_out), .out(sb),
    .sel(MemAddress[1:0]));
  Shifter #(.width(32)) shifter_4 (.in(bit_extender_2_out), .\dist (5'b01000), .out(shifter_4_out));
  Shifter #(.width(32)) shifter_5 (.in(bit_extender_2_out), .\dist (5'b10000), .out(shifter_5_out));
  Multiplexer #(.select(2), .width(32)) multiplexer_2 (
    .in0(bit_extender_2_out), .in1(shifter_4_out), .in2(shifter_5_out), .out(sh), .sel(MemAddress[1:0]));  // open: in3
  Multiplexer #(.select(2), .width(4)) multiplexer_3 (
    .in0(4'b0001), .in1(4'b0010), .in2(4'b0100), .in3(4'b1000), .out(sbmask), .sel(MemAddress[1:0]));
  Multiplexer #(.select(2), .width(4)) multiplexer_4 (
    .in0(4'b0011), .in1(4'b0110), .in2(4'b1100), .out(shmask), .sel(MemAddress[1:0]));  // open: in3
  Multiplexer #(.select(2), .width(32)) multiplexer_5 (
    .in0(sb), .in1(sh), .in2(DataFromReg), .out(DataToMem), .sel(Instruction[13:12]));  // open: in3
  Multiplexer #(.select(2), .width(4)) multiplexer_6 (
    .in0(sbmask), .in1(shmask), .in2(4'b1111), .out(multiplexer_6_out), .sel(Instruction[13:12]));  // open: in3
  assign bit_extender_3_out = {{3{MemRW}}, MemRW};  // Bit_Extender bit_extender_3
  assign MemWriteMask = bit_extender_3_out & multiplexer_6_out;  // AND_Gate and_1, 4 bits wide

  // Other names for the same wires on the sheet: func3[2:0] = Instruction[14:12]; func3_01[1:0] = Instruction[13:12];
  //   Sel[1:0] = MemAddress[1:0]; sw[31:0] = DataFromReg

  // Notes on the sheet:
  //   INPUTS to your circuit
  //   DON'T CHANGE THE LOCATIONS OF THE INPUTS AND OUTPUTS!
  //   OUTPUT from your circuit
endmodule
