// Logisim project regfile.circ as structural Verilog: 1 circuit, main circuit regfile
module regfile (
  input  [4:0] ReadIndex1,
  input  [4:0] ReadIndex2,
  input  [4:0] WriteIndex,
  input  [31:0] WriteData,
  input  RegWEn,
  input  clk,
  output [31:0] ra,
  output [31:0] sp,
  output [31:0] t0,
  output [31:0] t1,
  output [31:0] t2,
  output [31:0] s0,
  output [31:0] s1,
  output [31:0] a0,
  output [31:0] ReadData1,
  output [31:0] ReadData2
);

  wire and_1_out, and_2_out, and_3_out, and_4_out, and_5_out, and_6_out, and_7_out, and_8_out, and_9_out,
       and_10_out, and_11_out, and_12_out, and_13_out, and_14_out, and_15_out, and_16_out, and_17_out,
       and_18_out, and_19_out, and_20_out, and_21_out, and_22_out, and_23_out, and_24_out, and_25_out,
       and_26_out, and_27_out, and_28_out, and_29_out, and_30_out, and_31_out, comparator_1_eq,
       comparator_2_eq, comparator_3_eq, comparator_4_eq, comparator_5_eq, comparator_6_eq, comparator_7_eq,
       comparator_8_eq, comparator_9_eq, comparator_10_eq, comparator_11_eq, comparator_12_eq,
       comparator_13_eq, comparator_14_eq, comparator_15_eq, comparator_16_eq, comparator_17_eq,
       comparator_18_eq, comparator_19_eq, comparator_20_eq, comparator_21_eq, comparator_22_eq,
       comparator_23_eq, comparator_24_eq, comparator_25_eq, comparator_26_eq, comparator_27_eq,
       comparator_28_eq, comparator_29_eq, comparator_30_eq, comparator_31_eq;
  wire [31:0] reg3q, reg4q, reg11q, reg12q, reg13q, reg14q, reg15q, reg16q, reg17q, reg18q, reg19q, reg20q,
       reg21q, reg22q, reg23q, reg24q, reg25q, reg26q, reg27q, reg28q, reg29q, reg30q, reg31q, x0;

  Comparator #(.width(5)) comparator_1 (.a(WriteIndex), .b(5'b00001), .eq(comparator_1_eq));  // open: gt, lt
  Comparator #(.width(5)) comparator_2 (.a(WriteIndex), .b(5'b00010), .eq(comparator_2_eq));  // open: gt, lt
  Comparator #(.width(5)) comparator_3 (.a(WriteIndex), .b(5'b00011), .eq(comparator_3_eq));  // open: gt, lt
  Comparator #(.width(5)) comparator_4 (.a(WriteIndex), .b(5'b00100), .eq(comparator_4_eq));  // open: gt, lt
  Comparator #(.width(5)) comparator_5 (.a(WriteIndex), .b(5'b00101), .eq(comparator_5_eq));  // open: gt, lt
  Comparator #(.width(5)) comparator_6 (.a(WriteIndex), .b(5'b00110), .eq(comparator_6_eq));  // open: gt, lt
  Comparator #(.width(5)) comparator_7 (.a(WriteIndex), .b(5'b00111), .eq(comparator_7_eq));  // open: gt, lt
  Comparator #(.width(5)) comparator_8 (.a(WriteIndex), .b(5'b01000), .eq(comparator_8_eq));  // open: gt, lt
  Comparator #(.width(5)) comparator_9 (.a(WriteIndex), .b(5'b01001), .eq(comparator_9_eq));  // open: gt, lt
  Comparator #(.width(5)) comparator_10 (.a(WriteIndex), .b(5'b01010), .eq(comparator_10_eq));  // open: gt, lt
  Comparator #(.width(5)) comparator_11 (.a(WriteIndex), .b(5'b01011), .eq(comparator_11_eq));  // open: gt, lt
  Comparator #(.width(5)) comparator_12 (.a(WriteIndex), .b(5'b01100), .eq(comparator_12_eq));  // open: gt, lt
  Comparator #(.width(5)) comparator_13 (.a(WriteIndex), .b(5'b01101), .eq(comparator_13_eq));  // open: gt, lt
  Comparator #(.width(5)) comparator_14 (.a(WriteIndex), .b(5'b01110), .eq(comparator_14_eq));  // open: gt, lt
  Comparator #(.width(5)) comparator_15 (.a(WriteIndex), .b(5'b01111), .eq(comparator_15_eq));  // open: gt, lt
  Comparator #(.width(5)) comparator_16 (.a(WriteIndex), .b(5'b10000), .eq(comparator_16_eq));  // open: gt, lt
  Comparator #(.width(5)) comparator_17 (.a(WriteIndex), .b(5'b10001), .eq(comparator_17_eq));  // open: gt, lt
  Comparator #(.width(5)) comparator_18 (.a(WriteIndex), .b(5'b10010), .eq(comparator_18_eq));  // open: gt, lt
  Comparator #(.width(5)) comparator_19 (.a(WriteIndex), .b(5'b10011), .eq(comparator_19_eq));  // open: gt, lt
  Comparator #(.width(5)) comparator_20 (.a(WriteIndex), .b(5'b10100), .eq(comparator_20_eq));  // open: gt, lt
  Comparator #(.width(5)) comparator_21 (.a(WriteIndex), .b(5'b10101), .eq(comparator_21_eq));  // open: gt, lt
  Comparator #(.width(5)) comparator_22 (.a(WriteIndex), .b(5'b10110), .eq(comparator_22_eq));  // open: gt, lt
  Comparator #(.width(5)) comparator_23 (.a(WriteIndex), .b(5'b10111), .eq(comparator_23_eq));  // open: gt, lt
  Comparator #(.width(5)) comparator_24 (.a(WriteIndex), .b(5'b11000), .eq(comparator_24_eq));  // open: gt, lt
  Comparator #(.width(5)) comparator_25 (.a(WriteIndex), .b(5'b11001), .eq(comparator_25_eq));  // open: gt, lt
  Comparator #(.width(5)) comparator_26 (.a(WriteIndex), .b(5'b11010), .eq(comparator_26_eq));  // open: gt, lt
  Comparator #(.width(5)) comparator_27 (.a(WriteIndex), .b(5'b11011), .eq(comparator_27_eq));  // open: gt, lt
  Comparator #(.width(5)) comparator_28 (.a(WriteIndex), .b(5'b11100), .eq(comparator_28_eq));  // open: gt, lt
  Comparator #(.width(5)) comparator_29 (.a(WriteIndex), .b(5'b11101), .eq(comparator_29_eq));  // open: gt, lt
  Comparator #(.width(5)) comparator_30 (.a(WriteIndex), .b(5'b11110), .eq(comparator_30_eq));  // open: gt, lt
  Comparator #(.width(5)) comparator_31 (.a(WriteIndex), .b({5{1'b1}}), .eq(comparator_31_eq));  // open: gt, lt
  Register #(.width(32)) register_1 (.D({32{1'b0}}), .en(1'b0), .clk(clk), .Q(x0));  // open: clr
  Register #(.width(32)) register_2 (.D(WriteData), .en(and_1_out), .clk(clk), .Q(ra));  // open: clr
  and and_1 (and_1_out, comparator_1_eq, RegWEn);
  Register #(.width(32)) register_3 (.D(WriteData), .en(and_2_out), .clk(clk), .Q(sp));  // open: clr
  and and_2 (and_2_out, comparator_2_eq, RegWEn);
  Register #(.width(32)) register_4 (.D(WriteData), .en(and_3_out), .clk(clk), .Q(reg3q));  // open: clr
  and and_3 (and_3_out, comparator_3_eq, RegWEn);
  Register #(.width(32)) register_5 (.D(WriteData), .en(and_4_out), .clk(clk), .Q(reg4q));  // open: clr
  and and_4 (and_4_out, comparator_4_eq, RegWEn);
  Register #(.width(32)) register_6 (.D(WriteData), .en(and_5_out), .clk(clk), .Q(t0));  // open: clr
  and and_5 (and_5_out, comparator_5_eq, RegWEn);
  Register #(.width(32)) register_7 (.D(WriteData), .en(and_6_out), .clk(clk), .Q(t1));  // open: clr
  and and_6 (and_6_out, comparator_6_eq, RegWEn);
  Register #(.width(32)) register_8 (.D(WriteData), .en(and_7_out), .clk(clk), .Q(t2));  // open: clr
  and and_7 (and_7_out, comparator_7_eq, RegWEn);
  Register #(.width(32)) register_9 (.D(WriteData), .en(and_8_out), .clk(clk), .Q(s0));  // open: clr
  and and_8 (and_8_out, comparator_8_eq, RegWEn);
  Register #(.width(32)) register_10 (.D(WriteData), .en(and_9_out), .clk(clk), .Q(s1));  // open: clr
  and and_9 (and_9_out, comparator_9_eq, RegWEn);
  Register #(.width(32)) register_11 (.D(WriteData), .en(and_10_out), .clk(clk), .Q(a0));  // open: clr
  and and_10 (and_10_out, comparator_10_eq, RegWEn);
  Register #(.width(32)) register_12 (.D(WriteData), .en(and_11_out), .clk(clk), .Q(reg11q));  // open: clr
  and and_11 (and_11_out, comparator_11_eq, RegWEn);
  Register #(.width(32)) register_13 (.D(WriteData), .en(and_12_out), .clk(clk), .Q(reg12q));  // open: clr
  and and_12 (and_12_out, comparator_12_eq, RegWEn);
  Register #(.width(32)) register_14 (.D(WriteData), .en(and_13_out), .clk(clk), .Q(reg13q));  // open: clr
  and and_13 (and_13_out, comparator_13_eq, RegWEn);
  Register #(.width(32)) register_15 (.D(WriteData), .en(and_14_out), .clk(clk), .Q(reg14q));  // open: clr
  and and_14 (and_14_out, comparator_14_eq, RegWEn);
  Register #(.width(32)) register_16 (.D(WriteData), .en(and_15_out), .clk(clk), .Q(reg15q));  // open: clr
  and and_15 (and_15_out, comparator_15_eq, RegWEn);
  Register #(.width(32)) register_17 (.D(WriteData), .en(and_16_out), .clk(clk), .Q(reg16q));  // open: clr
  and and_16 (and_16_out, comparator_16_eq, RegWEn);
  Register #(.width(32)) register_18 (.D(WriteData), .en(and_17_out), .clk(clk), .Q(reg17q));  // open: clr
  and and_17 (and_17_out, comparator_17_eq, RegWEn);
  Register #(.width(32)) register_19 (.D(WriteData), .en(and_18_out), .clk(clk), .Q(reg18q));  // open: clr
  and and_18 (and_18_out, comparator_18_eq, RegWEn);
  Register #(.width(32)) register_20 (.D(WriteData), .en(and_19_out), .clk(clk), .Q(reg19q));  // open: clr
  and and_19 (and_19_out, comparator_19_eq, RegWEn);
  Register #(.width(32)) register_21 (.D(WriteData), .en(and_20_out), .clk(clk), .Q(reg20q));  // open: clr
  and and_20 (and_20_out, comparator_20_eq, RegWEn);
  Register #(.width(32)) register_22 (.D(WriteData), .en(and_21_out), .clk(clk), .Q(reg21q));  // open: clr
  and and_21 (and_21_out, comparator_21_eq, RegWEn);
  Register #(.width(32)) register_23 (.D(WriteData), .en(and_22_out), .clk(clk), .Q(reg22q));  // open: clr
  and and_22 (and_22_out, comparator_22_eq, RegWEn);
  Register #(.width(32)) register_24 (.D(WriteData), .en(and_23_out), .clk(clk), .Q(reg23q));  // open: clr
  and and_23 (and_23_out, comparator_23_eq, RegWEn);
  Register #(.width(32)) register_25 (.D(WriteData), .en(and_24_out), .clk(clk), .Q(reg24q));  // open: clr
  and and_24 (and_24_out, comparator_24_eq, RegWEn);
  Register #(.width(32)) register_26 (.D(WriteData), .en(and_25_out), .clk(clk), .Q(reg25q));  // open: clr
  and and_25 (and_25_out, comparator_25_eq, RegWEn);
  Register #(.width(32)) register_27 (.D(WriteData), .en(and_26_out), .clk(clk), .Q(reg26q));  // open: clr
  and and_26 (and_26_out, comparator_26_eq, RegWEn);
  Register #(.width(32)) register_28 (.D(WriteData), .en(and_27_out), .clk(clk), .Q(reg27q));  // open: clr
  and and_27 (and_27_out, comparator_27_eq, RegWEn);
  Register #(.width(32)) register_29 (.D(WriteData), .en(and_28_out), .clk(clk), .Q(reg28q));  // open: clr
  and and_28 (and_28_out, comparator_28_eq, RegWEn);
  Register #(.width(32)) register_30 (.D(WriteData), .en(and_29_out), .clk(clk), .Q(reg29q));  // open: clr
  and and_29 (and_29_out, comparator_29_eq, RegWEn);
  Register #(.width(32)) register_31 (.D(WriteData), .en(and_30_out), .clk(clk), .Q(reg30q));  // open: clr
  and and_30 (and_30_out, comparator_30_eq, RegWEn);
  Register #(.width(32)) register_32 (.D(WriteData), .en(and_31_out), .clk(clk), .Q(reg31q));  // open: clr
  and and_31 (and_31_out, comparator_31_eq, RegWEn);
  Multiplexer #(.select(5), .width(32)) multiplexer_1 (
    .in0(x0), .in1(ra), .in2(sp), .in3(reg3q), .in4(reg4q), .in5(t0), .in6(t1), .in7(t2), .in8(s0), .in9(s1),
    .in10(a0), .in11(reg11q), .in12(reg12q), .in13(reg13q), .in14(reg14q), .in15(reg15q), .in16(reg16q),
    .in17(reg17q), .in18(reg18q), .in19(reg19q), .in20(reg20q), .in21(reg21q), .in22(reg22q), .in23(reg23q),
    .in24(reg24q), .in25(reg25q), .in26(reg26q), .in27(reg27q), .in28(reg28q), .in29(reg29q), .in30(reg30q),
    .in31(reg31q), .out(ReadData1), .sel(ReadIndex1));
  Multiplexer #(.select(5), .width(32)) multiplexer_2 (
    .in0(x0), .in1(ra), .in2(sp), .in3(reg3q), .in4(reg4q), .in5(t0), .in6(t1), .in7(t2), .in8(s0), .in9(s1),
    .in10(a0), .in11(reg11q), .in12(reg12q), .in13(reg13q), .in14(reg14q), .in15(reg15q), .in16(reg16q),
    .in17(reg17q), .in18(reg18q), .in19(reg19q), .in20(reg20q), .in21(reg21q), .in22(reg22q), .in23(reg23q),
    .in24(reg24q), .in25(reg25q), .in26(reg26q), .in27(reg27q), .in28(reg28q), .in29(reg29q), .in30(reg30q),
    .in31(reg31q), .out(ReadData2), .sel(ReadIndex2));

  // Notes on the sheet:
  //   INPUTS to your circuit
  //   DON'T CHANGE THE LOCATIONS OF THE INPUTS AND OUTPUTS!
  //   These are DEBUG/TEST outputs from your circuit.
  //   OUTPUTS from your circuit
endmodule
