// Logisim project Itype.circ as structural Verilog: 1 circuit, main circuit main
module main (
);

  wire clk, control_logic_1_asel, control_logic_1_brun, control_logic_1_bsel, control_logic_1_memrw,
       control_logic_1_pcsel, control_logic_1_regwen, undriven, undriven_2;
  wire [1:0] control_logic_1_wbsel;
  wire [2:0] control_logic_1_immsel;
  wire [3:0] control_logic_1_alusel;
  wire [7:0] adder_1_out, Test;
  wire [31:0] a0, InputA, pc, ra, s0, s1, sp, t0, t1, t2;

  Clock clock_1 (.out(clk));
  Register register_1 (.D(adder_1_out), .clk(clk), .Q(Test));  // open: en, clr
  ROM #(.dataWidth(32)) rom_1 (.addr(Test), .data(InputA));
  Adder adder_1 (.a(8'h1), .b(Test), .out(adder_1_out));  // open: cin, cout
  // Probe on Test
  // Probe on InputA
  cpu cpu_1 (
    .clk(clk), .Instruction(InputA), .ProgramCounter(pc), .ra(ra), .sp(sp), .t0(t0), .t1(t1), .t2(t2),
    .s0(s0), .s1(s1), .a0(a0));  // open: MemReadData, MemAddress, MemWriteMask, MemWriteData
  // Probe on control_logic_1_pcsel
  // Probe on control_logic_1_regwen
  control_logic control_logic_1 (
    .Instruction(InputA), .BrEq(undriven), .BrLt(undriven_2), .PCSel(control_logic_1_pcsel),
    .RegWEn(control_logic_1_regwen), .ImmSel(control_logic_1_immsel), .BrUn(control_logic_1_brun),
    .ASel(control_logic_1_asel), .BSel(control_logic_1_bsel), .ALUSel(control_logic_1_alusel),
    .MemRW(control_logic_1_memrw), .WBSel(control_logic_1_wbsel));
  // Probe on control_logic_1_immsel
  // Probe on undriven
  // Probe on undriven_2
  // Probe on control_logic_1_brun
  // Probe on control_logic_1_asel
  // Probe on pc
  // Probe on ra
  // Probe on sp
  // Probe on t0
  // Probe on t1
  // Probe on t2
  // Probe on s0
  // Probe on s1
  // Probe on a0
  // Probe on control_logic_1_bsel
  // Probe on control_logic_1_alusel
  // Probe on control_logic_1_memrw
  // Probe on control_logic_1_wbsel

  // Notes on the sheet:
  //   contents of rom_1 (hex, n*v repeats v):
  //   ff628313 429313 f2a313 fff2c313 42d313 4042d313 552e313 f02f313
endmodule
