// Logisim project Rtype.circ as structural Verilog: 1 circuit, main circuit main
module main (
);

  wire clk;
  wire [7:0] adder_1_out, Test;
  wire [31:0] a0, InputA, pc, ra, s0, s1, sp, t0, t1, t2;

  Clock clock_1 (.out(clk));
  Register register_1 (.D(adder_1_out), .clk(clk), .Q(Test));  // open: en, clr
  ROM #(.dataWidth(32)) rom_1 (.addr(Test), .data(InputA));
  Adder adder_1 (.a(8'h1), .b(Test), .out(adder_1_out));  // open: cin, cout
  // Probe on Test
  // Probe on InputA
  cpu cpu_1 (
    .clk(clk), .Instruction(InputA), .ProgramCounter(pc), .ra(ra), .sp(sp), .t0(t0), .t1(t1), .t2(t2),
    .s0(s0), .s1(s1), .a0(a0));  // open: MemReadData, MemAddress, MemWriteMask, MemWriteData
  // Probe on pc
  // Probe on ra
  // Probe on sp
  // Probe on t0
  // Probe on t1
  // Probe on t2
  // Probe on s0
  // Probe on s1
  // Probe on a0

  // Notes on the sheet:
  //   contents of rom_1 (hex, n*v repeats v):
  //   a00293 ffc00313 200413 6284b3 406280b3 829133 5324b3 62c0b3 835133 408354b3 62e0b3 62f133 2830533
  //   28310b3 2833133
endmodule
